// Digital circuit ex3.dig as structural Verilog
module ex3 (
  input  [1:0] A,
  input  [1:0] B,
  output Y
);

  wire and_1_out, and_2_out, and_3_out, and_4_out, and_5_out, not_1_out, not_2_out, not_3_out, not_4_out;

  not not_1 (not_1_out, B[1]);
  and and_1 (and_1_out, A[1], A[0]);
  and and_2 (and_2_out, B[1], B[0]);
  not not_2 (not_2_out, B[1]);
  not not_3 (not_3_out, B[0]);
  and and_3 (and_3_out, A[1], not_1_out);
  not not_4 (not_4_out, and_2_out);
  and and_4 (and_4_out, A[0], not_2_out, not_3_out);
  and and_5 (and_5_out, and_1_out, not_4_out);
  or or_1 (Y, and_3_out, and_5_out, and_4_out);
endmodule

/* Test case EX3 Test:
A B Y 

 0b00 0b00 0
 0b00 0b01 0
 0b00 0b10 0
 0b00 0b11 0
 0b01 0b00 1
 0b01 0b01 0
 0b01 0b10 0
 0b01 0b11 0
 0b10 0b00 1
 0b10 0b01 1
 0b10 0b10 0
 0b10 0b11 0
 0b11 0b00 1
 0b11 0b01 1
 0b11 0b10 1
 0b11 0b11 0
*/
