// Digital circuit Lab02.dig as structural Verilog
module Lab02 (
  input  B,
  input  C,
  input  A,
  input  D,
  output Fa,
  output Fb,
  output Fc,
  output Fd,
  output Fe,
  output Fg,
  output Ff
);

  wire and_1_out, and_2_out, and_3_out, and_4_out, and_5_out, and_6_out, and_7_out, and_8_out, and_9_out,
       and_10_out, and_11_out, and_12_out, and_13_out, and_14_out, and_15_out, and_16_out, and_17_out,
       and_18_out, and_19_out, and_20_out, and_21_out, and_22_out, and_23_out, and_24_out, and_25_out,
       and_26_out, and_27_out, and_28_out, and_29_out, and_30_out, and_31_out, and_32_out, and_33_out,
       and_34_out, and_35_out, and_36_out, Not_A, Not_B, Not_C, Not_D;

  not not_1 (Not_A, A);
  not not_2 (Not_B, B);
  not not_3 (Not_C, C);
  not not_4 (Not_D, D);
  and and_1 (and_1_out, Not_D, C);
  and and_2 (and_2_out, B, C);
  and and_3 (and_3_out, Not_A, C);
  and and_4 (and_4_out, Not_B, Not_D);
  and and_5 (and_5_out, Not_A, B, D);
  and and_6 (and_6_out, A, Not_B, Not_C);
  and and_7 (and_7_out, Not_A, Not_B);
  and and_8 (and_8_out, Not_B, Not_D);
  and and_9 (and_9_out, Not_B, Not_C);
  and and_10 (and_10_out, Not_A, C, D);
  and and_11 (and_11_out, A, D, Not_C);
  and and_12 (and_12_out, Not_A, Not_D, Not_C);
  and and_13 (and_13_out, Not_A, Not_C);
  and and_14 (and_14_out, Not_A, D);
  and and_15 (and_15_out, Not_A, B);
  and and_16 (and_16_out, A, Not_B);
  and and_17 (and_17_out, Not_C, D);
  or or_1 (Fa, and_1_out, and_2_out, and_3_out, and_4_out, and_5_out, and_6_out);
  or or_2 (Fb, and_7_out, and_8_out, and_9_out, and_10_out, and_11_out, and_12_out);
  or or_3 (Fc, and_13_out, and_14_out, and_15_out, and_16_out, and_17_out);
  and and_18 (and_18_out, Not_C, A);
  and and_19 (and_19_out, Not_A, Not_B, Not_D);
  and and_20 (and_20_out, Not_B, D, C);
  and and_21 (and_21_out, D, B, Not_C);
  and and_22 (and_22_out, Not_D, B, C);
  and and_23 (and_23_out, Not_B, Not_D);
  and and_24 (and_24_out, A, B);
  and and_25 (and_25_out, C, Not_D);
  and and_26 (and_26_out, A, D, C);
  and and_27 (and_27_out, C, A);
  and and_28 (and_28_out, C, Not_D, B);
  and and_29 (and_29_out, A, Not_B, Not_C);
  and and_30 (and_30_out, B, Not_A, Not_C);
  and and_31 (and_31_out, Not_A, Not_D, Not_C);
  and and_32 (and_32_out, B, Not_C);
  and and_33 (and_33_out, Not_B, A);
  and and_34 (and_34_out, A, C);
  and and_35 (and_35_out, C, Not_D);
  and and_36 (and_36_out, C, Not_A, Not_B);
  or or_4 (Fd, and_18_out, and_19_out, and_20_out, and_21_out, and_22_out);
  or or_5 (Fe, and_23_out, and_24_out, and_25_out, and_26_out);
  or or_6 (Ff, and_27_out, and_28_out, and_29_out, and_30_out, and_31_out);
  or or_7 (Fg, and_32_out, and_33_out, and_34_out, and_35_out, and_36_out);
  Seven_Seg seven_seg_1 (.a(Fa), .b(Fb), .c(Fc), .d(Fd), .e(Fe), .f(Ff), .g(Fg), .dp(1'b0));
endmodule
