// Digital circuit register-file.dig as structural Verilog
module register_file (
  input  [4:0] ReadReg1,
  input  [4:0] ReadReg2,
  input  [4:0] WriteReg,
  input  [31:0] WriteData,
  input  RegWrite,
  input  Clock,
  output [31:0] ReadData1,
  output [31:0] ReadData2
);

  wire and_1_out, and_2_out, and_3_out, and_4_out, and_5_out, and_6_out, and_7_out, and_8_out, and_9_out,
       and_10_out, and_11_out, and_12_out, and_13_out, and_14_out, and_15_out, and_16_out, and_17_out,
       and_18_out, and_19_out, and_20_out, and_21_out, and_22_out, and_23_out, and_24_out, and_25_out,
       and_26_out, and_27_out, and_28_out, and_29_out, and_30_out, and_31_out, WR_0, WR_1, WR_2, WR_3, WR_4,
       WR_5, WR_6, WR_7, WR_8, WR_9, WR_10, WR_11, WR_12, WR_13, WR_14, WR_15, WR_16, WR_17, WR_18, WR_19,
       WR_20, WR_21, WR_22, WR_23, WR_24, WR_25, WR_26, WR_27, WR_28, WR_29, WR_30, WR_31;
  wire [31:0] Q1, Q2, Q3, Q4, Q5, Q6, Q7, Q8, Q9, Q10, Q11, Q12, Q13, Q14, Q15, Q16, Q17, Q18, Q19, Q20, Q21,
       Q22, Q23, Q24, Q25, Q26, Q27, Q28, Q29, Q30, Q31;

  Decoder #(.Selector_Bits(5)) decoder_1 (
    .sel(WriteReg), .out_0(WR_0), .out_1(WR_1), .out_2(WR_2), .out_3(WR_3), .out_4(WR_4), .out_5(WR_5),
    .out_6(WR_6), .out_7(WR_7), .out_8(WR_8), .out_9(WR_9), .out_10(WR_10), .out_11(WR_11), .out_12(WR_12),
    .out_13(WR_13), .out_14(WR_14), .out_15(WR_15), .out_16(WR_16), .out_17(WR_17), .out_18(WR_18),
    .out_19(WR_19), .out_20(WR_20), .out_21(WR_21), .out_22(WR_22), .out_23(WR_23), .out_24(WR_24),
    .out_25(WR_25), .out_26(WR_26), .out_27(WR_27), .out_28(WR_28), .out_29(WR_29), .out_30(WR_30),
    .out_31(WR_31));
  Multiplexer #(.Bits(32), .Selector_Bits(5)) multiplexer_1 (
    .sel(ReadReg1), .in_0({32{1'b0}}), .in_1(Q1), .in_2(Q2), .in_3(Q3), .in_4(Q4), .in_5(Q5), .in_6(Q6),
    .in_7(Q7), .in_8(Q8), .in_9(Q9), .in_10(Q10), .in_11(Q11), .in_12(Q12), .in_13(Q13), .in_14(Q14),
    .in_15(Q15), .in_16(Q16), .in_17(Q17), .in_18(Q18), .in_19(Q19), .in_20(Q20), .in_21(Q21), .in_22(Q22),
    .in_23(Q23), .in_24(Q24), .in_25(Q25), .in_26(Q26), .in_27(Q27), .in_28(Q28), .in_29(Q29), .in_30(Q30),
    .in_31(Q31), .out(ReadData1));
  Multiplexer #(.Selector_Bits(5), .Bits(32)) multiplexer_2 (
    .sel(ReadReg2), .in_0({32{1'b0}}), .in_1(Q1), .in_2(Q2), .in_3(Q3), .in_4(Q4), .in_5(Q5), .in_6(Q6),
    .in_7(Q7), .in_8(Q8), .in_9(Q9), .in_10(Q10), .in_11(Q11), .in_12(Q12), .in_13(Q13), .in_14(Q14),
    .in_15(Q15), .in_16(Q16), .in_17(Q17), .in_18(Q18), .in_19(Q19), .in_20(Q20), .in_21(Q21), .in_22(Q22),
    .in_23(Q23), .in_24(Q24), .in_25(Q25), .in_26(Q26), .in_27(Q27), .in_28(Q28), .in_29(Q29), .in_30(Q30),
    .in_31(Q31), .out(ReadData2));
  and and_1 (and_1_out, RegWrite, WR_1);
  and and_2 (and_2_out, RegWrite, WR_2);
  and and_3 (and_3_out, RegWrite, WR_3);
  and and_4 (and_4_out, RegWrite, WR_4);
  and and_5 (and_5_out, RegWrite, WR_5);
  and and_6 (and_6_out, RegWrite, WR_6);
  and and_7 (and_7_out, RegWrite, WR_7);
  and and_8 (and_8_out, RegWrite, WR_8);
  and and_9 (and_9_out, RegWrite, WR_9);
  and and_10 (and_10_out, RegWrite, WR_10);
  Register #(.Bits(32)) Register_1 (.D(WriteData), .C(Clock), .en(and_1_out), .Q(Q1));
  Register #(.Bits(32)) Register_2 (.D(WriteData), .C(Clock), .en(and_2_out), .Q(Q2));
  Register #(.Bits(32)) Register_3 (.D(WriteData), .C(Clock), .en(and_3_out), .Q(Q3));
  Register #(.Bits(32)) Register_4 (.D(WriteData), .C(Clock), .en(and_4_out), .Q(Q4));
  Register #(.Bits(32)) Register_5 (.D(WriteData), .C(Clock), .en(and_5_out), .Q(Q5));
  Register #(.Bits(32)) Register_6 (.D(WriteData), .C(Clock), .en(and_6_out), .Q(Q6));
  Register #(.Bits(32)) Register_7 (.D(WriteData), .C(Clock), .en(and_7_out), .Q(Q7));
  Register #(.Bits(32)) Register_8 (.D(WriteData), .C(Clock), .en(and_8_out), .Q(Q8));
  Register #(.Bits(32)) Register_9 (.D(WriteData), .C(Clock), .en(and_9_out), .Q(Q9));
  Register #(.Bits(32)) Register_10 (.D(WriteData), .C(Clock), .en(and_10_out), .Q(Q10));
  and and_11 (and_11_out, RegWrite, WR_11);
  and and_12 (and_12_out, RegWrite, WR_12);
  and and_13 (and_13_out, RegWrite, WR_13);
  and and_14 (and_14_out, RegWrite, WR_14);
  and and_15 (and_15_out, RegWrite, WR_15);
  and and_16 (and_16_out, RegWrite, WR_16);
  and and_17 (and_17_out, RegWrite, WR_17);
  and and_18 (and_18_out, RegWrite, WR_18);
  and and_19 (and_19_out, RegWrite, WR_19);
  and and_20 (and_20_out, RegWrite, WR_20);
  Register #(.Bits(32)) Register_11 (.D(WriteData), .C(Clock), .en(and_11_out), .Q(Q11));
  Register #(.Bits(32)) Register_12 (.D(WriteData), .C(Clock), .en(and_12_out), .Q(Q12));
  Register #(.Bits(32)) Register_13 (.D(WriteData), .C(Clock), .en(and_13_out), .Q(Q13));
  Register #(.Bits(32)) Register_14 (.D(WriteData), .C(Clock), .en(and_14_out), .Q(Q14));
  Register #(.Bits(32)) Register_15 (.D(WriteData), .C(Clock), .en(and_15_out), .Q(Q15));
  Register #(.Bits(32)) Register_16 (.D(WriteData), .C(Clock), .en(and_16_out), .Q(Q16));
  Register #(.Bits(32)) Register_17 (.D(WriteData), .C(Clock), .en(and_17_out), .Q(Q17));
  Register #(.Bits(32)) Register_18 (.D(WriteData), .C(Clock), .en(and_18_out), .Q(Q18));
  Register #(.Bits(32)) Register_19 (.D(WriteData), .C(Clock), .en(and_19_out), .Q(Q19));
  Register #(.Bits(32)) Register_20 (.D(WriteData), .C(Clock), .en(and_20_out), .Q(Q20));
  and and_21 (and_21_out, RegWrite, WR_21);
  and and_22 (and_22_out, RegWrite, WR_22);
  and and_23 (and_23_out, RegWrite, WR_23);
  and and_24 (and_24_out, RegWrite, WR_24);
  and and_25 (and_25_out, RegWrite, WR_25);
  and and_26 (and_26_out, RegWrite, WR_26);
  and and_27 (and_27_out, RegWrite, WR_27);
  and and_28 (and_28_out, RegWrite, WR_28);
  and and_29 (and_29_out, RegWrite, WR_29);
  and and_30 (and_30_out, RegWrite, WR_30);
  and and_31 (and_31_out, RegWrite, WR_31);
  Register #(.Bits(32)) Register_21 (.D(WriteData), .C(Clock), .en(and_21_out), .Q(Q21));
  Register #(.Bits(32)) Register_22 (.D(WriteData), .C(Clock), .en(and_22_out), .Q(Q22));
  Register #(.Bits(32)) Register_23 (.D(WriteData), .C(Clock), .en(and_23_out), .Q(Q23));
  Register #(.Bits(32)) Register_24 (.D(WriteData), .C(Clock), .en(and_24_out), .Q(Q24));
  Register #(.Bits(32)) Register_25 (.D(WriteData), .C(Clock), .en(and_25_out), .Q(Q25));
  Register #(.Bits(32)) Register_26 (.D(WriteData), .C(Clock), .en(and_26_out), .Q(Q26));
  Register #(.Bits(32)) Register_27 (.D(WriteData), .C(Clock), .en(and_27_out), .Q(Q27));
  Register #(.Bits(32)) Register_28 (.D(WriteData), .C(Clock), .en(and_28_out), .Q(Q28));
  Register #(.Bits(32)) Register_29 (.D(WriteData), .C(Clock), .en(and_29_out), .Q(Q29));
  Register #(.Bits(32)) Register_30 (.D(WriteData), .C(Clock), .en(and_30_out), .Q(Q30));
  Register #(.Bits(32)) Register_31 (.D(WriteData), .C(Clock), .en(and_31_out), .Q(Q31));

  // Other names for the same wires on the sheet: C = Clock; RD1[31:0] = ReadData1; RD2[31:0] = ReadData2;
  //   RR1[4:0] = ReadReg1; RR2[4:0] = ReadReg2; RW = RegWrite; WD[31:0] = WriteData; WR[4:0] = WriteReg
endmodule

/* Test case Register File Test:
WriteReg WriteData RegWrite Clock ReadReg1 ReadReg2 ReadData1 ReadData2

# $1 = 25
1 25 1 C 1 0 25 0

# $2 = 30
2 30 1 C 0 2 0 30

# $(N+1) = (N+1)
loop(N, 30)
	(N+1) (N+1) 1 C (N+1) (N) (N+1) (N)
end loop

# $(N+1) = N-60
loop(N, 30)
	(N+1) (N-60) 1 C (N+1) (N+1) (N-60) (N-60)
end loop

# Try writing to $0. This should not write anything
0 25 1 C 0 0 0 0

# try writing when RegWrite = 0
# (the registers should still have their old values)
loop(N, 30)
	(N+1) (N+80) 0 C (N+1) (N+1) (N-60) (N-60)
end loop
*/
